# Fritzing sketch newton (saved by Fritzing 0.9.3b)
circuit board: 8.47719cm x 5.84423cm
breadboards: 2

parts:
  VccLogique = DC Power [voltage=5]
  Vpower = DC Power [voltage=12V]  # not connected
  S1 = Square Pushbutton
  Composant1 = Arduino Nano (Rev3.0)
  DIP-Relay1 = DIP-Relay-D31A [part_number=D31A*]
  LEDCapteur = LED - 3mm [color="Green (570nm)" package="3 mm [THT]"]
  Q2 = NPN-Transistor [package="TO92 [THT]"]
  Q3 = NPN-Transistor [package="TO92 [THT]"]
  Q4 = TRANSISTOR_PNP [package=to-92]
  R2 = Resistor [tolerance=±5% resistance=330 package=THT]
  R3 = Resistor [tolerance=±5% resistance=330 package=THT]
  J8 = Power Jack [package=power_jack_pth]
  J9 = BANANA_CONN [package=banana_conn]
  J10 = BANANA_CONN [package=banana_conn]
  Photo1 = female pin header, 2 pins [form="♀ (female)"]
  Photo2 = female pin header, 2 pins [form="♀ (female)"]
  Laser1 = female pin header, 2 pins [form="♀ (female)"]
  Laser2 = female pin header, 2 pins [form="♀ (female)"]
  DistAlim = female pin header, 2 pins [form="♀ (female)"]
  DistI2C = female pin header, 2 pins [form="♀ (female)"]
  LEDBouton = LED - 3mm [color="Red (633nm)" package="3 mm [THT]"]
  RLed = Resistor [tolerance=±5% resistance=220 package=THT]

nets:
  GND: VccLogique.V-
  N1: S1.leg0, Composant1.D5
  GND_2: S1.leg1, Composant1.GND, Composant1.D9, DIP-Relay1.A1_Switch_Terminal_A, Q3.B, R2.Pin_0, J8.GND, Photo1.pin2, Photo2.pin1, Photo2.pin2, DistAlim.pin2, RLed.Pin_1
  N2: Composant1.D2, LEDBouton.anode
  N3: Composant1.D3, LEDCapteur.anode
  N4: Composant1.D4, Q4.B
  N5: Composant1.D10, R3.Pin_1, Photo1.pin1
  N6: Composant1.D12/MISO, Q2.C
  N7: Composant1.VIN, Q4.C, R2.Pin_1, R3.Pin_0, J8.PWR, Laser1.pin1, Laser2.pin1, DistAlim.pin1
  N8: Composant1.A5, DistI2C.pin2
  N9: Composant1.A4, DistI2C.pin1
  N10: DIP-Relay1.Coil2_-, J9.1
  N11: DIP-Relay1.B1_Switch_Terminal_B, J10.1
  N12: DIP-Relay1.A2_Switch_Terminal_A, Q4.E
  N13: LEDCapteur.cathode, LEDBouton.cathode, RLed.Pin_0
  N14: Q2.E, Laser2.pin2
  N15: Q3.E, Laser1.pin2
